# Fritzing sketch 光敏电阻控制LED (saved by Fritzing 0.9.3b)
breadboards: 1

parts:
  元件1 = Arduino Uno (Rev3)
  R1 = Photocell (LDR) [package=THT]
  R2 = Resistor [tolerance=±5% resistance=220 package=THT]
  LED1 = LED - 5mm [color="Red (633nm)" package="5 mm [THT]"]
  R3 = Resistor [tolerance=±5% resistance=220 package=THT]

nets:
  N1: 元件1.A0, R1.pin_0, R2.Pin_1
  N2: 元件1.D2, LED1.cathode
  N3: 元件1.5V, R1.pin_1
  N4: 元件1.GND, R2.Pin_0, R3.Pin_0
  N5: LED1.anode, R3.Pin_1
