# Fritzing sketch 开关控制LED开关 (saved by Fritzing 0.9.3b)
circuit board: 8.46667cm x 5.64444cm
breadboards: 1

parts:
  S1 = Pushbutton [package="[THT]"]
  LED1 = LED - 5mm [color="Red (633nm)" package="5 mm [THT]"]
  R1 = Resistor [tolerance=±5% resistance=220 package=THT]
  元件1 = Arduino Uno (Rev3)

nets:
  N1: S1.Pin_1, S1.Pin_2, S1.Pin_3, S1.Pin_4, 元件1.5V
  N2: LED1.cathode, 元件1.D12/MISO
  N3: LED1.anode, R1.Pin_0, 元件1.GND
  N4: R1.Pin_1, 元件1.D4

notes:
  开关正负极的接法，如果要使用pin获取开关的状态 一切要跨过电阻
