# Fritzing sketch LCD2 (saved by Fritzing 0.9.3b)
circuit board: 8.46667cm x 5.64444cm
breadboards: 1

parts:
  LCD1 = LCD screen
  元件1 = Arduino Uno (Rev3)
  R2 = Trimmer Potentiometer [maximum_resistance=10kΩ package=THT]

nets:
  VSS: LCD1.VSS, LCD1.R/W, LCD1.LED-, 元件1.GND, R2.leg2
  VDD: LCD1.VDD, 元件1.5V
  N1: LCD1.V0, R2.wiper
  N2: LCD1.RS, 元件1.D12/MISO
  N3: LCD1.E, 元件1.D11_PWM/MOSI
  N4: LCD1.DB4, 元件1.D5_PWM
  N5: LCD1.DB5, 元件1.D4
  N6: LCD1.DB6, 元件1.D3_PWM
  N7: LCD1.DB7, 元件1.D2
  N8: LCD1.LED+, 元件1.3V3

notes:
  LCD 4数字pin接法
